# Fritzing sketch stm32-drum (saved by Fritzing 0.9.3b)
breadboards: 2

parts:
  Part1 = Arduino Nano (Rev3.0)  # not connected
  U1 = STM32F103C8T6 blue mini board  # not connected
  Grove1 = Grove OLED 128x96  # not connected
  Part2 = FTDI Basic Programmer  # not connected
  R1 = Resistor [tolerance=±5% resistance=220 package="0603 [SMD]"]
  C1 = Capacitor [package=cap-pth-5mm]
  U3 = AUDIO-JACK2 [package=audio-jack]

nets:
  N1: R1.Pin_0, U3.TIP
  N2: R1.Pin_1, C1.2
  N3: C1.1, U3.SLEEVE
